# Fritzing sketch outdoor_mod (saved by Fritzing 0.8.5b)
breadboards: 1

parts:
  Part1 = Photon
  BMP1 = BMP085 Breakout  # not connected
  DS1 = DS18B20 1-Wire Temperature Sensor Probe Cable
  R1 = Resistor [tolerance=±5% resistance=10k package=THT]
  R2 = Resistor [tolerance=±5% resistance=10k package=THT]

nets:
  GND: Part1.GND, DS1.GND
  N1: Part1.D0, DS1.DQ, R2.Pin_1
  N2: Part1.D1, DS1.shield, R1.Pin_1
  3V3: Part1.3V3, DS1.VDD, R1.Pin_0, R2.Pin_0

notes:
  AOSONG AM2315

custom parts:
  BMP085 Breakout: A breakout for the BMP085 barometric pressure and temperature sensor
